// Logisim project test-circuit.circ as structural Verilog: 1 circuit, main circuit main
module main (
  input  in_1,
  input  in_2,
  input  in_3,
  input  in_4,
  input  in_5,
  input  in_6,
  input  in_7,
  input  in_8,
  input  in_9,
  input  in_10,
  input  in_11,
  input  in_12,
  input  in_13,
  input  in_14,
  input  in_15,
  input  in_16,
  input  \МКНФ ,
  input  \МКНФ_2 
);

  // truth_table truth_table_1: pin names not known; wires that end beside it: 16'ha3f6, 16'ha3f6, \МКНФ 
  // karnaugh_map karnaugh_map_1: pin names not known
  // truth_table truth_table_2: pin names not known; wires that end beside it: {in_1, in_2, in_4, in_3, in_5, in_6, in_8, in_7, in_13, in_14, in_16, in_15, in_9, in_10, in_12, in_11}, {in_1, in_2, in_4, in_3, in_5, in_6, in_8, in_7, in_13, in_14, in_16, in_15, in_9, in_10, in_12, in_11}
  // karnaugh_map karnaugh_map_2: pin names not known; wires that end beside it: \МКНФ_2 

  // Other names for the same wires on the sheet: a = in_11; b = in_12; c = in_10; d = in_9; e = in_15; f = in_16;
  //   g = in_14; h = in_13; i = in_7; j = in_8; k = in_6; l = in_5; m = in_3; n = in_4; o = in_2; p = in_1

  // Notes on the sheet:
  //   Функция может быть задана константой в векторном виде
  //   Или можно использовать панель для удобства
endmodule
